// Logisim project 2107086_ALU.circ as structural Verilog: 9 circuits, main circuit main
module main (
  input  Control_0,
  input  Control_1,
  input  Control_2,
  input  [17:0] A,
  input  [17:0] B,
  output [17:0] Result,
  output Zero,
  output Negative,
  output Carry,
  output Overflow
);

  wire [17:0] multiplexer_1_out, multiplexer_2_out, multiplexer_3_out, n18_bit_and_1_result,
       n18_bit_not_1_result, n18_bit_or_1_result, n18_bit_xor_1_result, n18bitadder_1_result;

  _18_bit_xor u_18_bit_xor_1 (.A(A), .B(B), .Result(n18_bit_xor_1_result));
  _18_bit_not u_18_bit_not_1 (.A(A), .Result(n18_bit_not_1_result));
  _18_bit_AND u_18_bit_and_1 (.A(A), .B(B), .Result(n18_bit_and_1_result));
  _18_bit_OR u_18_bit_or_1 (.A(A), .B(B), .Result(n18_bit_or_1_result));
  Multiplexer #(.width(18), .enable("false")) multiplexer_1 (
    .in0(n18_bit_xor_1_result), .in1(n18_bit_not_1_result), .out(multiplexer_1_out), .sel(Control_1));
  _18bitadder u_18bitadder_1 (
    .B(B), .A(A), .Mode(Control_0), .Carry(Carry), .Overflow(Overflow), .Result(n18bitadder_1_result));  // open: Sign
  Multiplexer #(.width(18), .enable("false")) multiplexer_2 (
    .in0(n18_bit_and_1_result), .in1(n18_bit_or_1_result), .out(multiplexer_2_out), .sel(Control_0));
  Multiplexer #(.width(18), .enable("false")) multiplexer_3 (
    .in0(multiplexer_2_out), .in1(n18bitadder_1_result), .out(multiplexer_3_out), .sel(Control_1));
  Multiplexer #(.width(18), .enable("false")) multiplexer_4 (
    .in0(multiplexer_3_out), .in1(multiplexer_1_out), .out(Result), .sel(Control_2));
  zero_negative zero_negative_1 (.A(Result), .Zero(Zero), .Negative(Negative));
endmodule

// AND
module _18_bit_AND (
  input  [17:0] A,
  input  [17:0] B,
  output [17:0] Result
);

  assign Result = A & B;  // AND_Gate and_1, 18 bits wide
endmodule

// OR
module _18_bit_OR (
  input  [17:0] A,
  input  [17:0] B,
  output [17:0] Result
);

  assign Result = A | B;  // OR_Gate or_1, 18 bits wide
endmodule

module _1_bit_adder (
  input  A,
  input  B,
  input  Cin,
  output S,
  output Cout
);

  wire and_1_out, and_2_out, xor_1_out;

  xor xor_1 (xor_1_out, A, B);
  and and_1 (and_1_out, xor_1_out, Cin);
  and and_2 (and_2_out, B, A);
  xor xor_2 (S, xor_1_out, Cin);
  or or_1 (Cout, and_1_out, and_2_out);
endmodule

// +/-
module _18_bit_adder_subtractor (
  input  Control,
  input  [17:0] A,
  input  [17:0] B,
  output [17:0] Result,
  output Carry,
  output Overflow
);

  wire [17:0] bit_extender_1_out, xor_1_out;

  assign bit_extender_1_out = {{17{Control}}, Control};  // Bit_Extender bit_extender_1
  assign xor_1_out = bit_extender_1_out ^ B;  // XOR_Gate xor_1, 18 bits wide
  _18bitadder u_18bitadder_1 (
    .B(xor_1_out), .A(A), .Mode(Control), .Carry(Carry), .Overflow(Overflow), .Result(Result));  // open: Sign
endmodule

module zero_negative (
  input  [17:0] A,
  output Zero,
  output Negative
);

  nor nor_1 (Zero, A[0], A[1], A[2], A[3], A[4], A[5], A[6], A[7], A[8], A[10], A[11], A[12], A[13], A[14], A[15], A[16], A[9], A[17]);

  assign Negative = A[17];
endmodule

// XOR
module _18_bit_xor (
  input  [17:0] A,
  input  [17:0] B,
  output [17:0] Result
);

  assign Result = A ^ B;  // XOR_Gate xor_1, 18 bits wide
endmodule

// NOT
module _18_bit_not (
  input  [17:0] A,
  output [17:0] Result
);

  assign Result = ~A;  // NOT_Gate not_1, 18 bits wide
endmodule

module _18bitadder (
  input  Mode,
  input  [17:0] B,
  input  [17:0] A,
  output [17:0] Result,
  output Sign,
  output Overflow,
  output Carry
);

  wire adder_1bit_1_carry, adder_1bit_2_carry, adder_1bit_3_carry, adder_1bit_4_carry, adder_1bit_5_carry,
       adder_1bit_6_carry, adder_1bit_7_carry, adder_1bit_8_carry, adder_1bit_9_carry, adder_1bit_10_carry,
       adder_1bit_11_carry, adder_1bit_12_carry, adder_1bit_13_carry, adder_1bit_14_carry,
       adder_1bit_15_carry, adder_1bit_16_carry, adder_1bit_17_carry, and_1_out, and_2_out, not_1_out,
       not_2_out, not_3_out;
  wire [17:0] complement_1_out_3;

  complement complement_1 (.Input(B), .Mode(Mode), .out_3(complement_1_out_3));
  Adder_1Bit adder_1bit_1 (
    .A(A[0]), .B(complement_1_out_3[0]), .Cin(Mode), .Carry(adder_1bit_1_carry), .Sum(Result[0]));
  Adder_1Bit adder_1bit_2 (
    .A(A[1]), .B(complement_1_out_3[1]), .Cin(adder_1bit_1_carry), .Carry(adder_1bit_2_carry), .Sum(Result[1]));
  Adder_1Bit adder_1bit_3 (
    .A(A[2]), .B(complement_1_out_3[2]), .Cin(adder_1bit_2_carry), .Carry(adder_1bit_3_carry), .Sum(Result[2]));
  Adder_1Bit adder_1bit_4 (
    .A(A[3]), .B(complement_1_out_3[3]), .Cin(adder_1bit_3_carry), .Carry(adder_1bit_4_carry), .Sum(Result[3]));
  Adder_1Bit adder_1bit_5 (
    .A(A[4]), .B(complement_1_out_3[4]), .Cin(adder_1bit_4_carry), .Carry(adder_1bit_5_carry), .Sum(Result[4]));
  Adder_1Bit adder_1bit_6 (
    .A(A[5]), .B(complement_1_out_3[5]), .Cin(adder_1bit_5_carry), .Carry(adder_1bit_6_carry), .Sum(Result[5]));
  Adder_1Bit adder_1bit_7 (
    .A(A[6]), .B(complement_1_out_3[6]), .Cin(adder_1bit_6_carry), .Carry(adder_1bit_7_carry), .Sum(Result[6]));
  Adder_1Bit adder_1bit_8 (
    .A(A[7]), .B(complement_1_out_3[7]), .Cin(adder_1bit_7_carry), .Carry(adder_1bit_8_carry), .Sum(Result[7]));
  Adder_1Bit adder_1bit_9 (
    .A(A[8]), .B(complement_1_out_3[8]), .Cin(adder_1bit_8_carry), .Carry(adder_1bit_9_carry), .Sum(Result[8]));
  Adder_1Bit adder_1bit_10 (
    .A(A[9]), .B(complement_1_out_3[9]), .Cin(adder_1bit_9_carry), .Carry(adder_1bit_10_carry),
    .Sum(Result[9]));
  Adder_1Bit adder_1bit_11 (
    .A(A[10]), .B(complement_1_out_3[10]), .Cin(adder_1bit_10_carry), .Carry(adder_1bit_11_carry),
    .Sum(Result[10]));
  Adder_1Bit adder_1bit_12 (
    .A(A[11]), .B(complement_1_out_3[11]), .Cin(adder_1bit_11_carry), .Carry(adder_1bit_12_carry),
    .Sum(Result[11]));
  Adder_1Bit adder_1bit_13 (
    .A(A[12]), .B(complement_1_out_3[12]), .Cin(adder_1bit_12_carry), .Carry(adder_1bit_13_carry),
    .Sum(Result[12]));
  Adder_1Bit adder_1bit_14 (
    .A(A[13]), .B(complement_1_out_3[13]), .Cin(adder_1bit_13_carry), .Carry(adder_1bit_14_carry),
    .Sum(Result[13]));
  Adder_1Bit adder_1bit_15 (
    .A(A[14]), .B(complement_1_out_3[14]), .Cin(adder_1bit_14_carry), .Carry(adder_1bit_15_carry),
    .Sum(Result[14]));
  Adder_1Bit adder_1bit_16 (
    .A(A[15]), .B(complement_1_out_3[15]), .Cin(adder_1bit_15_carry), .Carry(adder_1bit_16_carry),
    .Sum(Result[15]));
  Adder_1Bit adder_1bit_17 (
    .A(A[16]), .B(complement_1_out_3[16]), .Cin(adder_1bit_16_carry), .Carry(adder_1bit_17_carry),
    .Sum(Result[16]));
  Adder_1Bit adder_1bit_18 (
    .A(A[17]), .B(complement_1_out_3[17]), .Cin(adder_1bit_17_carry), .Carry(Carry), .Sum(Result[17]));
  not not_1 (not_1_out, complement_1_out_3[17]);
  not not_2 (not_2_out, A[17]);
  not not_3 (not_3_out, Result[17]);
  and and_1 (and_1_out, Result[17], not_1_out, not_2_out);
  and and_2 (and_2_out, complement_1_out_3[17], not_3_out, A[17]);
  or or_1 (Overflow, and_1_out, and_2_out);

  assign Sign = Result[17];
endmodule
